// Logisim project 25b6048_HalfAdder_Logisim.circ as structural Verilog: 1 circuit, main circuit main
module main (
  input  X,
  input  Y,
  output out_3,
  output out_4
);

  xor Sum (out_3, X, Y);
  and carry (out_4, X, Y);
endmodule
